// Logisim project main.circ as structural Verilog: 7 circuits, main circuit ULA-CELULA-4BIT
module MAIN (
  input  [3:0] A,
  input  [3:0] B,
  input  C,
  input  [2:0] S,
  output [3:0] SAIDA
);

  wire ula_celula_4bit_1_c_out, ula_celula_4bit_1_overflow;

  ULA_CELULA_4BIT ula_celula_4bit_1 (
    .A(A), .B(B), .SAIDA(SAIDA), .C_out(ula_celula_4bit_1_c_out), .OVERFLOW(ula_celula_4bit_1_overflow),
    .S0(S[0]), .S1(S[1]), .S2(S[2]));
  LED Cn_4 (.in(ula_celula_4bit_1_c_out));
  LED OVERFLOW (.in(ula_celula_4bit_1_overflow));

  // Notes on the sheet:
  //   Unidade Lógica e Aritmética
  //   S2    S1   S0
  //   0      0      0        CLEAR  
  //   0      0      1           DEF
  //   0      1      0           A - B
  //   0      1      1           A + B
  //   1      0      0         A xor B 
  //   1      0      1         A or B
  //   1      1      0        A and B
  //   1      1      1       PRESET
  //   Tabela de Operaçoes
  //   OPERAÇAO
endmodule

module ULA_CELULA_4BIT (
  input  [3:0] A,
  input  [3:0] B,
  input  S2,
  input  S1,
  input  S0,
  output [3:0] SAIDA,
  output C_out,
  output OVERFLOW
);

  wire not_1_out, ula_celula_1bit_1_c_out, ula_celula_1bit_2_c_out, ula_celula_1bit_3_c_out,
       ula_celula_1bit_4_c_out;

  ULA_CELULA_1BIT ula_celula_1bit_1 (
    .A(A[3]), .B(B[3]), .C_in(ula_celula_1bit_2_c_out), .C_out(ula_celula_1bit_1_c_out),
    .SEL_OP({S2, S1, S0}), .OUT_RESULT(SAIDA[3]));
  ULA_CELULA_1BIT ula_celula_1bit_2 (
    .A(A[2]), .B(B[2]), .C_in(ula_celula_1bit_3_c_out), .C_out(ula_celula_1bit_2_c_out),
    .SEL_OP({S2, S1, S0}), .OUT_RESULT(SAIDA[2]));
  OVERFLOW overflow_1 (
    .A(A[3]), .B(B[3]), .S(SAIDA[3]), .C_IN(ula_celula_1bit_1_c_out), .SELETOR({S2, S1, S0}),
    .OVERFLOW(OVERFLOW));
  ULA_CELULA_1BIT ula_celula_1bit_3 (
    .A(A[1]), .B(B[1]), .C_in(ula_celula_1bit_4_c_out), .C_out(ula_celula_1bit_3_c_out),
    .SEL_OP({S2, S1, S0}), .OUT_RESULT(SAIDA[1]));
  ULA_CELULA_1BIT ula_celula_1bit_4 (
    .A(A[0]), .B(B[0]), .C_out(ula_celula_1bit_4_c_out), .SEL_OP({S2, S1, S0}), .OUT_RESULT(SAIDA[0]));  // open: C_in
  not not_1 (not_1_out, S2);
  and AND (C_out, ula_celula_1bit_1_c_out, not_1_out);
  ULA_CELULA_1BIT ula_celula_1bit_5 ();  // open: A, B, C_in, C_out, SEL_OP, OUT_RESULT

  // Notes on the sheet:
  //   S2    S1   S0
  //   0      0      0        CLEAR  
  //   0      0      1           DEF
  //   0      1      0           A - B
  //   0      1      1           A + B
  //   1      0      0         A xor B 
  //   1      0      1         A or B
  //   1      1      0        A and B
  //   1      1      1       PRESET
  //   OPERAÇAO
endmodule

module ULA_CELULA_1BIT (
  input  A,
  input  B,
  input  C_in,
  input  [2:0] SEL_OP,
  output OUT_RESULT,
  output C_out
);

  wire adder_1_cout, adder_1_out, AND_2_out, AND_out, clear_1_out_3, definir_1_out_3, OR_out, preset_1_out_3,
       subtractor_1_bout, subtractor_1_out, XOR_out;

  CLEAR clear_1 (.in_1(A), .in_2(B), .out_3(clear_1_out_3));
  DEFINIR definir_1 (.in_1(A), .out_3(definir_1_out_3), .in_2(B));
  PRESET preset_1 (.in_1(A), .out_3(preset_1_out_3), .in_2(B));
  Adder #(.width(1)) adder_1 (.a(A), .b(B), .out(adder_1_out), .cin(C_in), .cout(adder_1_cout));
  Subtractor #(.width(1)) subtractor_1 (.a(A), .b(B), .out(subtractor_1_out), .bin(C_in), .bout(subtractor_1_bout));
  xor XOR (XOR_out, A, B);
  or OR (OR_out, A, B);
  and AND (AND_out, A, B);
  Multiplexer #(.select(3), .enable("false")) multiplexer_1 (
    .in0(clear_1_out_3), .in1(definir_1_out_3), .in2(adder_1_out), .in3(subtractor_1_out), .in4(XOR_out),
    .in5(OR_out), .in6(AND_out), .in7(preset_1_out_3), .out(OUT_RESULT), .sel(SEL_OP));
  and AND_2 (AND_2_out, SEL_OP[2], ~SEL_OP[1], ~SEL_OP[0]);  // AND_Gate
  Multiplexer #(.enable("false")) multiplexer_2 (
    .in0(adder_1_cout), .in1(subtractor_1_bout), .out(C_out), .sel(AND_2_out));
endmodule

module CLEAR (
  input  in_1,
  input  in_2,
  output out_3
);


  assign out_3 = 1'b0;
endmodule

module PRESET (
  input  in_1,
  input  in_2,
  output out_3
);


  assign out_3 = 1'b1;
endmodule

module DEFINIR (
  input  in_1,
  input  in_2,
  output out_3
);

  wire not_1_out, not_2_out;

  not not_1 (not_1_out, in_1);
  not not_2 (not_2_out, in_2);
  nand nand_1 (out_3, not_1_out, not_2_out);
endmodule

module OVERFLOW (
  input  A,
  input  B,
  input  S,
  input  C_IN,
  input  [2:0] SELETOR,
  output OVERFLOW
);

  wire AND_2_out, AND_3_out, AND_out, OR_out;

  and AND (AND_out, SELETOR[0], SELETOR[1]);  // AND_Gate
  and AND_2 (AND_2_out, ~A, S, ~B);  // AND_Gate
  and AND_3 (AND_3_out, A, ~S, B);  // AND_Gate
  or OR (OR_out, AND_2_out, AND_3_out);
  Multiplexer #(.enable("false")) multiplexer_1 (.in0(OR_out), .in1(C_IN), .out(OVERFLOW), .sel(AND_out));
endmodule
